// Logisim project alu.circ as structural Verilog: 5 circuits, main circuit main
module main (
  input  [31:0] A,
  input  [31:0] B,
  input  [3:0] ALUSel,
  output [31:0] Result,
  output OverFlow,
  output Zero
);

  wire adder_1_cout, adder_2_cout, comparator_1_lt, comparator_2_lt, not_1_out, or_2_out, xor_2_out;
  wire [4:0] selector5_1_out_2, selector5_2_out_2, selector5_3_out_2;
  wire [30:0] selector31_1_out_2, selector31_2_out_2;
  wire [31:0] adder_1_out, and_1_out, bit_extender_1_out, bit_extender_2_out, multiplier_1_out,
       multiplier_2_cout, or_1_out, shifter_1_out, shifter_2_out, shifter_3_out, subtractor_1_out,
       unsignedmultiplier_1_out_3, xor_1_out;

  Comparator #(.width(32), .mode("unsigned")) comparator_1 (.a(A), .b(B), .lt(comparator_1_lt));  // open: gt, eq
  assign bit_extender_1_out = {{31{1'b0}}, comparator_1_lt};  // Bit_Extender bit_extender_1
  Adder #(.width(32)) adder_1 (.a(A), .b(B), .out(adder_1_out), .cin(1'b0), .cout(adder_1_cout));
  selector5 selector5_1 (.in_1(B), .out_2(selector5_1_out_2));
  selector5 selector5_2 (.in_1(B), .out_2(selector5_2_out_2));
  selector5 selector5_3 (.in_1(B), .out_2(selector5_3_out_2));
  Shifter #(.width(32)) shifter_1 (.in(A), .\dist (selector5_1_out_2), .out(shifter_1_out));
  assign bit_extender_2_out = {{31{1'b0}}, comparator_2_lt};  // Bit_Extender bit_extender_2
  Comparator #(.width(32)) comparator_2 (.a(A), .b(B), .lt(comparator_2_lt));  // open: gt, eq
  assign xor_1_out = A ^ B;  // XOR_Gate xor_1, 32 bits wide
  Shifter #(.width(32), .shift("lr")) shifter_2 (.in(A), .\dist (selector5_2_out_2), .out(shifter_2_out));
  assign or_1_out = A | B;  // OR_Gate or_1, 32 bits wide
  assign and_1_out = A & B;  // AND_Gate and_1, 32 bits wide
  Multiplier #(.width(32)) multiplier_1 (.a(A), .b(B), .out(multiplier_1_out));  // open: cin, cout
  Multiplier #(.width(32)) multiplier_2 (.a(A), .b(B), .cout(multiplier_2_cout));  // open: out, cin
  UnsignedMultiplier unsignedmultiplier_1 (.in_1(A), .in_2(B), .out_3(unsignedmultiplier_1_out_3));
  Subtractor #(.width(32)) subtractor_1 (.a(A), .b(B), .out(subtractor_1_out), .bin(1'b0));  // open: bout
  Shifter #(.width(32), .shift("ar")) shifter_3 (.in(A), .\dist (selector5_3_out_2), .out(shifter_3_out));
  selector31 selector31_1 (.in_1(A), .out_2(selector31_1_out_2));
  selector31 selector31_2 (.in_1(B), .out_2(selector31_2_out_2));
  mux mux_1 (
    ._0(adder_1_out), ._1(shifter_1_out), ._2(bit_extender_2_out), ._3(bit_extender_1_out), ._4(xor_1_out),
    ._5(shifter_2_out), ._6(or_1_out), ._7(and_1_out), ._8(multiplier_1_out), ._9(multiplier_2_cout),
    ._10({32{1'b0}}), ._11(unsignedmultiplier_1_out_3), ._12(subtractor_1_out), ._13(shifter_3_out),
    ._14({32{1'b0}}), ._15(B), .a4(ALUSel[3]), .a3(ALUSel[2]), .a2(ALUSel[1]), .a1(ALUSel[0]), .out_21(Result));
  Adder #(.width(31)) adder_2 (
    .a(selector31_1_out_2), .b(selector31_2_out_2), .cin(1'b0), .cout(adder_2_cout));  // open: out
  not not_1 (not_1_out, or_2_out);
  or or_2 (or_2_out, ALUSel[0], ALUSel[1], ALUSel[2], ALUSel[3]);
  Comparator #(.width(32)) comparator_3 (.a(Result), .b({32{1'b0}}), .eq(Zero));  // open: gt, lt
  xor xor_2 (xor_2_out, adder_2_cout, adder_1_cout);
  and and_2 (OverFlow, xor_2_out, not_1_out);
endmodule

module mux (
  input  [31:0] _0,
  input  [31:0] _1,
  input  [31:0] _2,
  input  [31:0] _3,
  input  [31:0] _4,
  input  [31:0] _5,
  input  [31:0] _6,
  input  [31:0] _7,
  input  [31:0] _8,
  input  [31:0] _9,
  input  [31:0] _10,
  input  [31:0] _11,
  input  [31:0] _12,
  input  [31:0] _13,
  input  [31:0] _14,
  input  [31:0] _15,
  input  a4,
  input  a3,
  input  a2,
  input  a1,
  output [31:0] out_21
);

  wire and_1_out, and_2_out, and_3_out, and_4_out, and_5_out, and_6_out, and_7_out, and_8_out, and_9_out,
       and_10_out, and_11_out, and_12_out, and_13_out, and_14_out, and_15_out, and_16_out, not_1_out,
       not_2_out, not_3_out, not_4_out;
  wire [31:0] and_17_out, and_18_out, and_19_out, and_20_out, and_21_out, and_22_out, and_23_out, and_24_out,
       and_25_out, and_26_out, and_27_out, and_28_out, and_29_out, and_30_out, and_31_out, and_32_out,
       bit_extender_1_out, bit_extender_2_out, bit_extender_3_out, bit_extender_4_out, bit_extender_5_out,
       bit_extender_6_out, bit_extender_7_out, bit_extender_8_out, bit_extender_9_out, bit_extender_10_out,
       bit_extender_11_out, bit_extender_12_out, bit_extender_13_out, bit_extender_14_out,
       bit_extender_15_out, bit_extender_16_out;

  not not_1 (not_1_out, a4);
  not not_2 (not_2_out, a3);
  not not_3 (not_3_out, a2);
  not not_4 (not_4_out, a1);
  and and_1 (and_1_out, not_4_out, not_3_out, not_2_out, not_1_out);
  and and_2 (and_2_out, a1, not_3_out, not_2_out, not_1_out);
  and and_3 (and_3_out, not_4_out, a2, not_2_out, not_1_out);
  and and_4 (and_4_out, a1, a2, not_2_out, not_1_out);
  and and_5 (and_5_out, not_4_out, not_3_out, a3, not_1_out);
  and and_6 (and_6_out, a1, not_3_out, a3, not_1_out);
  and and_7 (and_7_out, not_4_out, a2, a3, not_1_out);
  and and_8 (and_8_out, a1, a2, a3, not_1_out);
  and and_9 (and_9_out, not_4_out, not_3_out, not_2_out, a4);
  and and_10 (and_10_out, a1, not_3_out, not_2_out, a4);
  and and_11 (and_11_out, not_4_out, a2, not_2_out, a4);
  and and_12 (and_12_out, a1, a2, not_2_out, a4);
  and and_13 (and_13_out, not_4_out, not_3_out, a3, a4);
  and and_14 (and_14_out, a1, not_3_out, a3, a4);
  and and_15 (and_15_out, not_4_out, a2, a3, a4);
  and and_16 (and_16_out, a1, a2, a3, a4);
  assign bit_extender_1_out = {{31{and_1_out}}, and_1_out};  // Bit_Extender bit_extender_1
  assign bit_extender_2_out = {{31{and_2_out}}, and_2_out};  // Bit_Extender bit_extender_2
  assign bit_extender_3_out = {{31{and_3_out}}, and_3_out};  // Bit_Extender bit_extender_3
  assign bit_extender_4_out = {{31{and_4_out}}, and_4_out};  // Bit_Extender bit_extender_4
  assign bit_extender_5_out = {{31{and_5_out}}, and_5_out};  // Bit_Extender bit_extender_5
  assign bit_extender_6_out = {{31{and_6_out}}, and_6_out};  // Bit_Extender bit_extender_6
  assign bit_extender_7_out = {{31{and_7_out}}, and_7_out};  // Bit_Extender bit_extender_7
  assign bit_extender_8_out = {{31{and_8_out}}, and_8_out};  // Bit_Extender bit_extender_8
  assign bit_extender_9_out = {{31{and_9_out}}, and_9_out};  // Bit_Extender bit_extender_9
  assign bit_extender_10_out = {{31{and_10_out}}, and_10_out};  // Bit_Extender bit_extender_10
  assign bit_extender_11_out = {{31{and_11_out}}, and_11_out};  // Bit_Extender bit_extender_11
  assign bit_extender_12_out = {{31{and_12_out}}, and_12_out};  // Bit_Extender bit_extender_12
  assign bit_extender_13_out = {{31{and_13_out}}, and_13_out};  // Bit_Extender bit_extender_13
  assign bit_extender_14_out = {{31{and_14_out}}, and_14_out};  // Bit_Extender bit_extender_14
  assign bit_extender_15_out = {{31{and_15_out}}, and_15_out};  // Bit_Extender bit_extender_15
  assign bit_extender_16_out = {{31{and_16_out}}, and_16_out};  // Bit_Extender bit_extender_16
  assign and_17_out = bit_extender_1_out & _0;  // AND_Gate and_17, 32 bits wide
  assign and_18_out = bit_extender_2_out & _1;  // AND_Gate and_18, 32 bits wide
  assign and_19_out = bit_extender_3_out & _2;  // AND_Gate and_19, 32 bits wide
  assign and_20_out = bit_extender_4_out & _3;  // AND_Gate and_20, 32 bits wide
  assign and_21_out = bit_extender_5_out & _4;  // AND_Gate and_21, 32 bits wide
  assign and_22_out = bit_extender_6_out & _5;  // AND_Gate and_22, 32 bits wide
  assign and_23_out = bit_extender_7_out & _6;  // AND_Gate and_23, 32 bits wide
  assign and_24_out = bit_extender_8_out & _7;  // AND_Gate and_24, 32 bits wide
  assign and_25_out = bit_extender_9_out & _8;  // AND_Gate and_25, 32 bits wide
  assign and_26_out = bit_extender_10_out & _9;  // AND_Gate and_26, 32 bits wide
  assign and_27_out = bit_extender_11_out & _10;  // AND_Gate and_27, 32 bits wide
  assign and_28_out = bit_extender_12_out & _11;  // AND_Gate and_28, 32 bits wide
  assign and_29_out = bit_extender_13_out & _12;  // AND_Gate and_29, 32 bits wide
  assign and_30_out = bit_extender_14_out & _13;  // AND_Gate and_30, 32 bits wide
  assign and_31_out = bit_extender_15_out & _14;  // AND_Gate and_31, 32 bits wide
  assign and_32_out = bit_extender_16_out & _15;  // AND_Gate and_32, 32 bits wide
  assign out_21 = and_17_out | and_18_out | and_19_out | and_20_out | and_21_out | and_22_out | and_23_out | and_24_out | and_25_out | and_26_out | and_27_out | and_28_out | and_29_out | and_30_out | and_31_out | and_32_out;  // OR_Gate or_1, 32 bits wide
endmodule

module selector5 (
  input  [31:0] in_1,
  output [4:0] out_2
);


  assign out_2 = in_1[4:0];
endmodule

module selector31 (
  input  [31:0] in_1,
  output [30:0] out_2
);


  assign out_2 = in_1[30:0];
endmodule

module UnsignedMultiplier (
  input  [31:0] in_1,
  input  [31:0] in_2,
  output [31:0] out_3
);

  wire adder_2_cout, adder_4_cout, and_1_out;
  wire [31:0] adder_2_out, adder_3_out, adder_5_out, and_2_out, and_3_out, bit_extender_1_out,
       bit_extender_2_out, bit_extender_3_out, bit_extender_4_out, bit_extender_5_out, multiplier_1_cout,
       multiplier_1_out, shifter_1_out, shifter_2_out, shifter_3_out, shifter_4_out, shifter_5_out;

  assign bit_extender_1_out = {{31{1'b0}}, and_1_out};  // Bit_Extender bit_extender_1
  and and_1 (and_1_out, in_1[31], in_2[31]);
  Shifter #(.width(32)) shifter_1 (.in(bit_extender_1_out), .\dist (5'b11110), .out(shifter_1_out));
  Adder #(.width(32)) adder_1 (.a(shifter_1_out), .b(adder_5_out), .out(out_3));  // open: cin, cout
  Shifter #(.width(32), .shift("lr")) shifter_2 (.in(and_3_out), .\dist (5'b00001), .out(shifter_2_out));
  Shifter #(.width(32)) shifter_3 (.in(and_3_out), .\dist ({5{1'b1}}), .out(shifter_3_out));
  Shifter #(.width(32), .shift("lr")) shifter_4 (.in(and_2_out), .\dist (5'b00001), .out(shifter_4_out));
  Shifter #(.width(32)) shifter_5 (.in(and_2_out), .\dist ({5{1'b1}}), .out(shifter_5_out));
  assign bit_extender_2_out = {{1{1'b0}}, in_1[30:0]};  // Bit_Extender bit_extender_2
  assign bit_extender_3_out = {{1{1'b0}}, in_2[30:0]};  // Bit_Extender bit_extender_3
  assign bit_extender_4_out = {{31{in_1[31]}}, in_1[31]};  // Bit_Extender bit_extender_4
  assign bit_extender_5_out = {{31{in_2[31]}}, in_2[31]};  // Bit_Extender bit_extender_5
  assign and_2_out = bit_extender_5_out & bit_extender_2_out;  // AND_Gate and_2, 32 bits wide
  assign and_3_out = bit_extender_4_out & bit_extender_3_out;  // AND_Gate and_3, 32 bits wide
  Multiplier #(.width(32)) multiplier_1 (
    .a(bit_extender_2_out), .b(bit_extender_3_out), .out(multiplier_1_out), .cout(multiplier_1_cout));  // open: cin
  Adder #(.width(32)) adder_2 (
    .a(multiplier_1_out), .b(shifter_3_out), .out(adder_2_out), .cin(1'b0), .cout(adder_2_cout));
  Adder #(.width(32)) adder_3 (
    .a(multiplier_1_cout), .b(shifter_2_out), .out(adder_3_out), .cin(adder_2_cout));  // open: cout
  Adder #(.width(32)) adder_4 (.a(adder_2_out), .b(shifter_5_out), .cin(1'b0), .cout(adder_4_cout));  // open: out
  Adder #(.width(32)) adder_5 (
    .a(adder_3_out), .b(shifter_4_out), .out(adder_5_out), .cin(adder_4_cout));  // open: cout
endmodule
