// Logisim project processor.circ as structural Verilog: 7 circuits, main circuit main
module main (
  input  in_1,
  output out_2,
  output [4:0] RS1,
  output EX_SEL,
  output [31:0] PC,
  output [31:0] INSTRUCTION,
  output [31:0] OP1,
  output [31:0] OP2,
  output [31:0] ALU_RES,
  output [4:0] RS2,
  output [3:0] ALU_OP,
  output ALU_SRC,
  output MEM_WRITE,
  output REG_WRITE,
  output [4:0] RD,
  output MEM_READ,
  output BRANCH,
  output MEM_TO_REG
);

  wire and_1_out, and_2_out, clock_1_out, not_1_out, undriven;
  wire [1:0] control_1_alu_op;
  wire [31:0] adder_1_out, adder_2_out, imm_gen_1_i_immediate, imm_gen_1_s_immediate, imm_gen_1_sb_immediate,
       main_1_read_data_2_b1228a6a, multiplexer_1_out, multiplexer_3_out, multiplexer_4_out, ram_1_dout;

  Register #(.width(32)) register_1 (.D(multiplexer_3_out), .en(undriven), .clk(clock_1_out), .Q(PC), .clr(in_1));
  Clock clock_1 (.out(clock_1_out));
  ROM #(.addrWidth(24), .dataWidth(32)) rom_1 (.addr(PC[25:2]), .data(INSTRUCTION));
  Clock sysclk ();  // open: out
  Adder #(.width(32)) adder_1 (.a(PC), .b(32'h4), .out(adder_1_out));  // open: cin, cout
  Imm_Gen imm_gen_1 (
    .INSTRUCTION(INSTRUCTION), .S_IMMEDIATE(imm_gen_1_s_immediate), .SB_IMMEDIATE(imm_gen_1_sb_immediate),
    .I_IMMEDIATE(imm_gen_1_i_immediate));
  control control_1 (
    .OP_CODE(INSTRUCTION[6:0]), .Mem_write(MEM_WRITE), .Branch(BRANCH), .Mem_Read(MEM_READ),
    .Mem_to_Reg(MEM_TO_REG), .Reg_write(REG_WRITE), .ALU_Src(ALU_SRC), .ex_sel(EX_SEL),
    .ALU_Op(control_1_alu_op));
  Multiplexer #(.width(32)) multiplexer_1 (
    .in0(imm_gen_1_i_immediate), .in1(imm_gen_1_s_immediate), .out(multiplexer_1_out), .sel(EX_SEL));  // open: en
  register_main main_1 (
    .Write_Data_6dfac92a(multiplexer_4_out), .Read_Data_1_766914a9(OP1),
    .Read_Data_2_b1228a6a(main_1_read_data_2_b1228a6a), .Read_Register_1_rs1_85912ed8(INSTRUCTION[19:15]),
    .Read_Register_2_rs2_a0541b39(INSTRUCTION[24:20]), .Write_Register_rd_3156e259(INSTRUCTION[11:7]),
    .RegWEn(REG_WRITE), .in_1(clock_1_out));
  Adder #(.width(32)) adder_2 (.a(PC), .b(imm_gen_1_sb_immediate), .out(adder_2_out));  // open: cin, cout
  not not_1 (not_1_out, ALU_SRC);
  Multiplexer #(.width(32)) multiplexer_2 (
    .in0(main_1_read_data_2_b1228a6a), .in1(multiplexer_1_out), .out(OP2), .sel(ALU_SRC));  // open: en
  and and_1 (and_1_out, not_1_out, INSTRUCTION[30]);
  Multiplexer #(.width(32)) multiplexer_3 (
    .in0(adder_1_out), .in1(adder_2_out), .out(multiplexer_3_out), .sel(and_2_out));  // open: en
  ALU_Control_d6e93f56 alu_control_d6e93f56_1 (
    .FUNC3(INSTRUCTION[14:12]), .ALU_Op(control_1_alu_op), .ALU_Sel(ALU_OP), .FUNC7(and_1_out));
  and and_2 (and_2_out, BRANCH, out_2);
  alu_main main_2 (.A(OP1), .B(OP2), .Result(ALU_RES), .Zero(out_2), .ALUSel(ALU_OP));  // open: OverFlow
  RAM #(.addrWidth(24), .dataWidth(32), .trigger("falling"), .databus("bibus")) ram_1 (
    .addr(ALU_RES[23:0]), .we(MEM_WRITE), .oe(MEM_READ), .clk(clock_1_out),
    .din(main_1_read_data_2_b1228a6a), .dout(ram_1_dout));
  Multiplexer #(.width(32)) multiplexer_4 (
    .in0(ALU_RES), .in1(ram_1_dout), .out(multiplexer_4_out), .sel(MEM_TO_REG));  // open: en

  assign RD = INSTRUCTION[11:7];
  assign RS1 = INSTRUCTION[19:15];
  assign RS2 = INSTRUCTION[24:20];

  // Other names for the same wires on the sheet: INS[31:0] = INSTRUCTION

  // Notes on the sheet:
  //   Reset
  //   contents of rom_1 (hex, n*v repeats v):
  //   130313 c828293 c838393 532423 530463 728a63 1432383 6440413 6448493 a50513 410113 5303b3 405303b3
  //   812423 5313b3 5323b3 5333b3 5343b3 5353b3 5363b3 5373b3 1032393 1033393 6434393 6436393 6437393
  //   1031393 1035393
  //   PC
  //   PC Src
  //   BRANCH
  //   ALU-CONTROL
endmodule

module Imm_Gen (
  input  [31:0] INSTRUCTION,
  output [31:0] S_IMMEDIATE,
  output [31:0] SB_IMMEDIATE,
  output [31:0] I_IMMEDIATE
);

  wire [11:5] undriven;

  assign S_IMMEDIATE = {{20{undriven[11]}}, {undriven, INSTRUCTION[11:7]}};  // Bit_Extender bit_extender_1
  assign SB_IMMEDIATE = {{19{INSTRUCTION[31]}}, {INSTRUCTION[31], INSTRUCTION[7], INSTRUCTION[30:25], INSTRUCTION[11:8], 1'b0}};  // Bit_Extender bit_extender_2
  assign I_IMMEDIATE = {{20{INSTRUCTION[31]}}, INSTRUCTION[31:20]};  // Bit_Extender bit_extender_3
endmodule

module Instruction_type_decode (
  input  [6:0] OP_CODE,
  output R,
  output L,
  output S,
  output Branch,
  output I
);

  Comparator #(.width(7), .mode("unsigned")) comparator_1 (.a(7'b0110011), .b(OP_CODE), .eq(R));  // open: gt, lt
  Comparator #(.width(7), .mode("unsigned")) comparator_2 (.a(7'b0000011), .b(OP_CODE), .eq(L));  // open: gt, lt
  Comparator #(.width(7), .mode("unsigned")) comparator_3 (.a(7'b0100011), .b(OP_CODE), .eq(S));  // open: gt, lt
  Comparator #(.width(7), .mode("unsigned")) comparator_4 (.a(7'b1100011), .b(OP_CODE), .eq(Branch));  // open: gt, lt
  Comparator #(.width(7), .mode("unsigned")) comparator_5 (.a(7'b0010011), .b(OP_CODE), .eq(I));  // open: gt, lt

  // Notes on the sheet:
  //   R-Type
  //   Load
  //   Store
  //   I-Type
endmodule

module control_decode_e902778d (
  input  R,
  input  L,
  input  S,
  input  B,
  input  I,
  output Mem_write,
  output Branch,
  output Mem_Read,
  output Mem_to_Reg,
  output Reg_write,
  output [1:0] ALU_Op,
  output ALU_Src,
  output ex_sel
);

  wire not_1_out, or_1_out;

  or or_1 (or_1_out, I, L);
  or or_2 (Reg_write, R, L, I);
  ALU_OP alu_op_1 (.R(R), .L(L), .S(S), .B(B), .I(I), .ALU_OP(ALU_Op));
  or or_3 (ALU_Src, I, S, L);
  not not_1 (not_1_out, or_1_out);
  and and_1 (ex_sel, not_1_out, S);

  assign Branch = B;
  assign Mem_Read = L;
  assign Mem_to_Reg = L;
  assign Mem_write = S;

  // Notes on the sheet:
  //   R-type
  //   Load
  //   Store
  //   Branch
  //   I-type
endmodule

module ALU_OP (
  input  R,
  input  L,
  input  S,
  input  B,
  input  I,
  output [1:0] ALU_OP
);

  wire not_1_out, not_2_out, not_3_out, or_1_out, or_2_out;

  or or_1 (or_1_out, L, S);
  not not_1 (not_1_out, B);
  or or_2 (or_2_out, R, I);
  not not_2 (not_2_out, or_1_out);
  not not_3 (not_3_out, or_2_out);
  and and_1 (ALU_OP[1], or_2_out, not_2_out, not_1_out);
  and and_2 (ALU_OP[0], not_3_out, not_2_out, B);

  // Notes on the sheet:
  //   R-type
  //   Load
  //   Store
  //   Branch
  //   I-Type
  //   Alu-Op
endmodule

module control (
  input  [6:0] OP_CODE,
  output Mem_write,
  output Branch,
  output Mem_Read,
  output Mem_to_Reg,
  output Reg_write,
  output [1:0] ALU_Op,
  output ALU_Src,
  output ex_sel
);

  wire instruction_type_decode_1_branch, instruction_type_decode_1_i, instruction_type_decode_1_l,
       instruction_type_decode_1_r, instruction_type_decode_1_s;

  Instruction_type_decode instruction_type_decode_1 (
    .OP_CODE(OP_CODE), .R(instruction_type_decode_1_r), .L(instruction_type_decode_1_l),
    .S(instruction_type_decode_1_s), .Branch(instruction_type_decode_1_branch),
    .I(instruction_type_decode_1_i));
  control_decode_e902778d control_decode_e902778d_1 (
    .Mem_write(Mem_write), .Branch(Branch), .Mem_Read(Mem_Read), .Mem_to_Reg(Mem_to_Reg),
    .Reg_write(Reg_write), .ALU_Src(ALU_Src), .ex_sel(ex_sel), .R(instruction_type_decode_1_r),
    .L(instruction_type_decode_1_l), .S(instruction_type_decode_1_s), .B(instruction_type_decode_1_branch),
    .I(instruction_type_decode_1_i), .ALU_Op(ALU_Op));

  // Notes on the sheet:
  //   Instruction-Opcode
endmodule

module ALU_Control_d6e93f56 (
  input  [2:0] FUNC3,
  input  FUNC7,
  input  [1:0] ALU_Op,
  output [3:0] ALU_Sel
);

  wire and_1_out, and_2_out, and_3_out, and_4_out, and_5_out, and_6_out, and_7_out, and_8_out, and_9_out,
       and_10_out, and_11_out, and_12_out, and_13_out, and_14_out, and_15_out, and_16_out, and_17_out,
       and_18_out, and_19_out, and_20_out, and_21_out, and_22_out, not_1_out, not_2_out, not_3_out,
       not_4_out, not_5_out, not_6_out, not_7_out, not_8_out, not_9_out, not_10_out, not_11_out, not_12_out,
       not_13_out, not_14_out, not_15_out, not_16_out, not_17_out, or_1_out, or_2_out;

  not not_1 (not_1_out, ALU_Op[1]);
  not not_2 (not_2_out, ALU_Op[0]);
  not not_3 (not_3_out, ALU_Op[0]);
  not not_4 (not_4_out, ALU_Op[1]);
  and and_1 (and_1_out, ALU_Op[1], not_2_out);
  not not_5 (not_5_out, FUNC3[2]);
  and and_2 (and_2_out, ALU_Op[0], not_1_out);
  not not_6 (not_6_out, FUNC3[0]);
  not not_7 (not_7_out, FUNC3[1]);
  not not_8 (not_8_out, FUNC3[2]);
  not not_9 (not_9_out, FUNC3[1]);
  not not_10 (not_10_out, FUNC3[0]);
  not not_11 (not_11_out, FUNC3[2]);
  not not_12 (not_12_out, FUNC3[0]);
  and and_3 (and_3_out, not_3_out, not_4_out);
  and and_4 (and_4_out, FUNC3[0], not_9_out, not_5_out);
  and and_5 (and_5_out, not_10_out, FUNC3[1], not_11_out);
  not not_13 (not_13_out, FUNC3[2]);
  not not_14 (not_14_out, FUNC3[1]);
  and and_6 (and_6_out, not_6_out, not_7_out, not_8_out);
  and and_7 (and_7_out, FUNC3[0], FUNC3[1], not_13_out);
  and and_8 (and_8_out, not_12_out, not_14_out, FUNC3[2]);
  not not_15 (not_15_out, FUNC3[1]);
  not not_16 (not_16_out, FUNC3[0]);
  and and_9 (and_9_out, FUNC3[0], not_15_out, FUNC3[2]);
  and and_10 (and_10_out, FUNC7, and_6_out);
  and and_11 (and_11_out, not_16_out, FUNC3[1], FUNC3[2]);
  and and_12 (and_12_out, FUNC3[0], FUNC3[1], FUNC3[2]);
  and and_13 (and_13_out, and_1_out, and_10_out);
  not not_17 (not_17_out, FUNC7);
  and and_14 (and_14_out, and_6_out, not_17_out);
  or or_1 (or_1_out, and_2_out, and_13_out);
  and and_15 (and_15_out, and_14_out, and_1_out);
  and and_16 (and_16_out, and_4_out, and_1_out);
  and and_17 (and_17_out, and_1_out, and_5_out);
  and and_18 (and_18_out, and_1_out, and_7_out);
  and and_19 (and_19_out, and_1_out, and_8_out);
  and and_20 (and_20_out, and_1_out, and_9_out);
  and and_21 (and_21_out, and_1_out, and_11_out);
  and and_22 (and_22_out, and_1_out, and_12_out);
  or or_2 (or_2_out, and_3_out, and_15_out);
  Priority_Encoder #(.select(4)) priority_encoder_1 (
    .in0(or_2_out), .in1(and_16_out), .in2(and_17_out), .in3(and_18_out), .in4(and_19_out), .in5(and_20_out),
    .in6(and_21_out), .in7(and_22_out), .in8(1'b0), .in9(1'b0), .in10(1'b0), .in11(1'b0), .in12(or_1_out),
    .in13(1'b0), .in14(1'b0), .in15(1'b0), .out(ALU_Sel));  // open: gs, en_out, en_in

  // Notes on the sheet:
  //   ALU-Op
  //   Func-7
  //   Func-3
  //   R-Type/I-Type
  //   Branch
  //   load/store
  //   ADD/SUB
  //   SUB
  //   ADD
  //   SUB
  //   SLL
  //   SLTU
  //   XOR
  //   SRL
  //   OR
  //   AND
  //   SLT
  //   ADD
  //   ALU-Sel
endmodule
