// Logisim project register.circ as structural Verilog: 1 circuit, main circuit main
module main (
  input  in_1,
  input  [31:0] Write_Data_6dfac92a,
  input  [4:0] Read_Register_1_rs1_85912ed8,
  input  [4:0] Read_Register_2_rs2_a0541b39,
  input  RegWEn,
  input  [4:0] Write_Register_rd_3156e259,
  output [31:0] Read_Data_1_766914a9,
  output [31:0] Read_Data_2_b1228a6a
);

  wire and_2_out, and_3_out, and_4_out, and_5_out, and_6_out, and_7_out, and_8_out, and_9_out,
       decoder_1_out0, decoder_1_out1, decoder_1_out2, decoder_1_out5, decoder_1_out6, decoder_1_out7,
       decoder_1_out8, decoder_1_out9, decoder_1_out10, undriven;
  wire [31:0] X1, X2, X5, X6, X7, X8, X9, X10, XO;

  Decoder #(.select(5)) decoder_1 (
    .out0(decoder_1_out0), .out1(decoder_1_out1), .out2(decoder_1_out2), .out5(decoder_1_out5),
    .out6(decoder_1_out6), .out7(decoder_1_out7), .out8(decoder_1_out8), .out9(decoder_1_out9),
    .out10(decoder_1_out10), .sel(Write_Register_rd_3156e259));  // open: out3, out4, out11, out12, out13, out14, out15, out16, out17, out18, out19, out20, out21, out22, out23, out24, out25, out26, out27, out28, out29, out30, out31, en
  // AND_Gate and_1 has open pins: in0=decoder_1_out0, in1=RegWEn, out=open
  and and_2 (and_2_out, decoder_1_out1, RegWEn);
  and and_3 (and_3_out, decoder_1_out2, RegWEn);
  and and_4 (and_4_out, decoder_1_out5, RegWEn);
  and and_5 (and_5_out, decoder_1_out6, RegWEn);
  and and_6 (and_6_out, decoder_1_out7, RegWEn);
  and and_7 (and_7_out, decoder_1_out8, RegWEn);
  and and_8 (and_8_out, decoder_1_out9, RegWEn);
  and and_9 (and_9_out, decoder_1_out10, RegWEn);
  Register #(.width(32)) u_X1 (.D(Write_Data_6dfac92a), .en(and_2_out), .clk(in_1), .Q(X1), .clr(undriven));
  Register #(.width(32)) u_X5 (.D(Write_Data_6dfac92a), .en(and_4_out), .clk(in_1), .Q(X5));  // open: clr
  Register #(.width(32)) u_X7 (.D(Write_Data_6dfac92a), .en(and_6_out), .clk(in_1), .Q(X7));  // open: clr
  Register #(.width(32)) u_X9 (.D(Write_Data_6dfac92a), .en(and_8_out), .clk(in_1), .Q(X9));  // open: clr
  Register #(.width(32)) u_XO (.D(Write_Data_6dfac92a), .en(1'b0), .clk(in_1), .Q(XO));  // open: clr
  Register #(.width(32)) u_X2 (.D(Write_Data_6dfac92a), .en(and_3_out), .clk(in_1), .Q(X2));  // open: clr
  Register #(.width(32)) u_X6 (.D(Write_Data_6dfac92a), .en(and_5_out), .clk(in_1), .Q(X6));  // open: clr
  Register #(.width(32)) u_X8 (.D(Write_Data_6dfac92a), .en(and_7_out), .clk(in_1), .Q(X8));  // open: clr
  Register #(.width(32)) u_X10 (.D(Write_Data_6dfac92a), .en(and_9_out), .clk(in_1), .Q(X10));  // open: clr
  Multiplexer #(.select(5), .width(32)) multiplexer_1 (
    .in0(XO), .in1(X1), .in2(X2), .in3({32{1'b0}}), .in4({32{1'b0}}), .in5(X5), .in6(X6), .in7(X7), .in8(X8),
    .in9(X9), .in10(X10), .in11({32{1'b0}}), .in12({32{1'b0}}), .in13({32{1'b0}}), .in14({32{1'b0}}),
    .in15({32{1'b0}}), .in16({32{1'b0}}), .in17({32{1'b0}}), .in18({32{1'b0}}), .in19({32{1'b0}}),
    .in20({32{1'b0}}), .in21({32{1'b0}}), .in22({32{1'b0}}), .in23({32{1'b0}}), .in24({32{1'b0}}),
    .in25({32{1'b0}}), .in26({32{1'b0}}), .in27({32{1'b0}}), .in28({32{1'b0}}), .in29({32{1'b0}}),
    .in30({32{1'b0}}), .in31({32{1'b0}}), .out(Read_Data_1_766914a9), .sel(Read_Register_1_rs1_85912ed8));  // open: en
  Multiplexer #(.select(5), .width(32)) multiplexer_2 (
    .in0(XO), .in1(X1), .in2(X2), .in3({32{1'b0}}), .in4({32{1'b0}}), .in5(X5), .in6(X6), .in7(X7), .in8(X8),
    .in9(X9), .in10(X10), .in11({32{1'b0}}), .in12({32{1'b0}}), .in13({32{1'b0}}), .in14({32{1'b0}}),
    .in15({32{1'b0}}), .in16({32{1'b0}}), .in17({32{1'b0}}), .in18({32{1'b0}}), .in19({32{1'b0}}),
    .in20({32{1'b0}}), .in21({32{1'b0}}), .in22({32{1'b0}}), .in23({32{1'b0}}), .in24({32{1'b0}}),
    .in25({32{1'b0}}), .in26({32{1'b0}}), .in27({32{1'b0}}), .in28({32{1'b0}}), .in29({32{1'b0}}),
    .in30({32{1'b0}}), .in31({32{1'b0}}), .out(Read_Data_2_b1228a6a), .sel(Read_Register_2_rs2_a0541b39));  // open: en

  // Notes on the sheet:
  //   Clock
endmodule
